# Fritzing sketch schematic (saved by Fritzing 0.9.3b)
breadboards: 1

parts:
  U1 = NodeMCU V3.0
  S1 = Pushbutton [package="[THT]"]
  R1 = Resistor [tolerance=±5% resistance=10k package=THT]

nets:
  N1: U1.3V3, S1.Pin_3, S1.Pin_4
  N2: U1.GND#6, U1.GND#13, U1.GND#16, U1.GND#33
  N3: U1.D5, S1.Pin_1, S1.Pin_2, R1.Pin_0
  N4: U1.GND#41, R1.Pin_1

custom parts:
  NodeMCU V3.0: ESP8266 based NodeMCU
