# Fritzing sketch Sketch (saved by Fritzing 0.9.3b)
breadboards: 1

parts:
  U1 = NodeMCU V1.0
  S1 = Pushbutton [package="[THT]"]
  R1 = Resistor [tolerance=±5% resistance=10k package=THT]
  U2 = mystery part, 5 pins [chip_label=MAX7219]

nets:
  N1: U1.D0, U1.RST
  N2: U1.D1, U1.3V3, S1.Pin_1, S1.Pin_2, U2.pin1
  N3: U1.D4, U2.pin3
  N4: U1.GND, R1.Pin_0, U2.pin2
  N5: U1.D5, U2.pin4
  N6: U1.D7, U2.pin5
  N7: S1.Pin_3, S1.Pin_4, R1.Pin_1

notes:
  Matrix Bot GIT: https://goo.gl/TAq3YG

custom parts:
  NodeMCU V1.0: ESP8266 based NodeMCU
